// Logisim project 658_Computer.circ as structural Verilog: 3 circuits, main circuit Microcontroller
module Motherboard (
);

  wire TIMING_rst, TIMING_rst_1;
  wire [9:0] TIMING_selector;

  Timing_Circuit TIMING (.SELECTOR(TIMING_selector), .RST(TIMING_rst), .RST_1(TIMING_rst_1));  // open: CLK, CLK_B
  Microcontroller microcontroller_1 (.SELECTOR(TIMING_selector), .RST(TIMING_rst), .RST_1(TIMING_rst_1));
endmodule

module Microcontroller (
  input  [9:0] SELECTOR,
  input  RST,
  input  RST_1
);

  wire A_128K, A_128K_B, and_1_out, and_3_out, and_4_out, and_5_out, and_6_out, and_8_out, and_10_out,
       and_11_out, BANK_LATCH, BANK_MAP, CS0_B, CS1_B, CS2_B, CS3_B, DATA_TRANS_B, DEVICE_B, IDEVICE_0,
       IDMEM_KERNAL_MODE_B, IDMEM_OUT_INTERRUPTS_B, IDMEM_USER_BANK_B, IREAD_ENABLE, IREAD_ENABLE_B,
       IREAD_SELECT, IRQ_B, IWRITE_ENABLE, IWRITE_ENABLE_B, IWRITE_SELECT, KERNAL_MODE, KERNAL_MODE_B,
       microprocessor_w65c816_1_p8, microprocessor_w65c816_1_p13, microprocessor_w65c816_1_p14,
       MRAM_ACCESS_B, MRAM_VALID, MRAM_VALID_B, MREAD, MREADY, MVALID, MWRITE, n8_bit_bi_latch_lvc543_1_p5,
       n8_bit_bi_latch_lvc543_1_p7, n16_bit_line_driver_lvc16244_4_p3, n16_bit_line_driver_lvc16244_4_p4,
       nand_4_out, nand_5_out, nand_8_out, nand_9_out, nand_10_out, nand_11_out, NMI_B, nor_2_out, nor_3_out,
       nor_4_out, not_1_out, not_2_out, not_3_out, not_4_out, not_5_out, not_6_out, not_7_out, not_8_out,
       not_9_out, not_10_out, not_13_out, not_16_out, not_17_out, not_18_out, not_19_out, not_20_out,
       or_3_out, or_4_out, or_5_out, or_6_out, or_7_out, or_9_out, or_10_out, PHI2, pull_resistor_2_node,
       pull_resistor_3_node, pull_resistor_4_node, pull_resistor_5_node, pull_resistor_10_node,
       pull_resistor_11_node, pull_resistor_12_node, pull_resistor_14_node, pull_resistor_15_node,
       pull_resistor_16_node, pull_resistor_19_node, pull_resistor_20_node, pull_resistor_21_node, RDY, READ,
       RESET, VALID_ADDRESS, VDA, VP_B, VPA, WRITE;
  wire [2:0] n8_bit_latch_lvc573_1_p2;
  wire [7:0] A0_7, A8_15, BA0_7, D, IRAM_A0_7, MRAM_A16_23, n8_bit_bi_latch_lvc543_1_p8, OUT_INTERRUPTS,
       ram_2_data, USER_BANK;
  wire [7:1] n3_to_8_decoder_lvc138_2_p5;
  wire [7:2] n3_to_8_decoder_lvc138_1_p5;
  wire [7:4] n3_to_8_decoder_lvc138_3_p6;
  wire [9:0] timing_circuit_1_selector;
  wire [16:0] IRAM_A;
  wire [23:0] MRAM_A;

  Timing_Circuit timing_circuit_1 (
    .SELECTOR({timing_circuit_1_selector[9], MRAM_ACCESS_B, timing_circuit_1_selector[7:0]}), .RST(RESET));  // open: RST_1, CLK, CLK_B
  Pull_Resistor #(.pull(1)) pull_resistor_1 (.node(NMI_B));
  not not_1 (not_1_out, VP_B);
  // Probe on A0_7
  // Probe on {4'b0000, n8_bit_latch_lvc573_1_p2, A0_7[0]}
  and and_1 (and_1_out, A0_7[1], A0_7[2], A0_7[3], not_1_out);
  not not_2 (not_2_out, A8_15[3]);
  not not_3 (not_3_out, BA0_7[0]);
  not not_4 (not_4_out, BA0_7[1]);
  not not_5 (not_5_out, BA0_7[2]);
  not not_6 (not_6_out, BA0_7[3]);
  not not_7 (not_7_out, BA0_7[4]);
  not not_8 (not_8_out, BA0_7[5]);
  not not_9 (not_9_out, BA0_7[6]);
  not not_10 (not_10_out, BA0_7[7]);
  Pull_Resistor #(.pull(1)) pull_resistor_2 (.node(pull_resistor_2_node));
  and and_2 (PHI2, timing_circuit_1_selector[0], timing_circuit_1_selector[1]);
  not not_11 (BANK_LATCH, timing_circuit_1_selector[1]);
  nand nand_1 (DATA_TRANS_B, timing_circuit_1_selector[0], timing_circuit_1_selector[1], timing_circuit_1_selector[3]);
  not not_12 (BANK_MAP, timing_circuit_1_selector[3]);
  nand nand_2 (IWRITE_SELECT, timing_circuit_1_selector[7], MRAM_ACCESS_B);
  nand nand_3 (IREAD_SELECT, MRAM_ACCESS_B, timing_circuit_1_selector[7], timing_circuit_1_selector[9]);
  not not_13 (not_13_out, nand_4_out);
  nand nand_4 (nand_4_out, and_1_out, ~IRQ_B);  // NAND_Gate
  Pull_Resistor pull_resistor_3 (.node(pull_resistor_3_node));
  Pull_Resistor pull_resistor_4 (.node(pull_resistor_4_node));
  and and_3 (and_3_out, A8_15[4], A8_15[5], A8_15[6], A8_15[7]);
  and and_4 (and_4_out, not_4_out, not_5_out, not_6_out);
  and and_5 (and_5_out, not_3_out, not_4_out, not_5_out, not_6_out);
  and and_6 (and_6_out, not_7_out, not_8_out, not_9_out, not_10_out);
  nand nand_5 (nand_5_out, A0_7[7], A8_15[0], A8_15[1], A8_15[2]);
  // _3_to_8_Decoder__LVC138 3_to_8_decoder_lvc138_1: pin names not known; wires that end beside it: IDEVICE_0, A0_7[3], A0_7[2:0], pull_resistor_2_node, {n3_to_8_decoder_lvc138_1_p5[7:4], IDMEM_OUT_INTERRUPTS_B, n3_to_8_decoder_lvc138_1_p5[2], IDMEM_USER_BANK_B, IDMEM_KERNAL_MODE_B}, n3_to_8_decoder_lvc138_1_p5[2]
  // _8_bit_Line_Driver__LVC541 8_bit_line_driver_lvc541_1: pin names not known; wires that end beside it: not_13_out, not_13_out, A0_7, IRAM_A0_7
  // _8_bit_Latch__LVC573 8_bit_latch_lvc573_1: pin names not known; wires that end beside it: nand_4_out, {4'b0000, n8_bit_latch_lvc573_1_p2, A0_7[0]}, pull_resistor_3_node, IRAM_A0_7
  // _8_to_3_Encoder__LS148 8_to_3_encoder_ls148_1: pin names not known; wires that end beside it: pull_resistor_4_node, {8{1'b1}}, n8_bit_latch_lvc573_1_p2, IRQ_B
  // _3_to_8_Decoder__LVC138 3_to_8_decoder_lvc138_2: pin names not known; wires that end beside it: KERNAL_MODE_B, DEVICE_B, A0_7[6:4], nand_5_out, {n3_to_8_decoder_lvc138_2_p5, IDEVICE_0}
  Pull_Resistor #(.pull(1)) pull_resistor_5 (.node(pull_resistor_5_node));
  // Probe on IRAM_A0_7
  nand nand_6 (DEVICE_B, not_2_out, and_3_out, and_6_out, and_5_out);
  nand nand_7 (A_128K_B, and_4_out, and_6_out);
  and and_7 (A_128K, and_4_out, and_6_out);
  // Microprocessor__W65C816 microprocessor_w65c816_1: pin names not known; wires that end beside it: pull_resistor_5_node, IRQ_B, NMI_B, RESET, PHI2, 64'h239093209053202, {A8_15, A0_7}, microprocessor_w65c816_1_p8, READ, RDY, VDA, VPA, microprocessor_w65c816_1_p13, microprocessor_w65c816_1_p14, VP_B
  Clock clock_1 (.out(microprocessor_w65c816_1_p14));
  not not_14 (WRITE, READ);
  Pull_Resistor pull_resistor_6 (.node(VDA));
  Pull_Resistor pull_resistor_7 (.node(VPA));
  // Probe on {A8_15, A0_7}
  // Probe on microprocessor_w65c816_1_p8
  Pull_Resistor #(.pull(1)) pull_resistor_8 (.node(microprocessor_w65c816_1_p13));
  Pull_Resistor #(.pull(1)) pull_resistor_9 (.node(VP_B));
  or or_1 (VALID_ADDRESS, VDA, VPA);
  and and_8 (and_8_out, IREAD_SELECT, READ, VALID_ADDRESS);
  and and_9 (IWRITE_ENABLE, IWRITE_SELECT, WRITE, VALID_ADDRESS);
  nor nor_1 (IREAD_ENABLE_B, and_8_out, BANK_MAP);
  or or_2 (IREAD_ENABLE, and_8_out, BANK_MAP);
  not not_15 (IWRITE_ENABLE_B, IWRITE_ENABLE);
  Pull_Resistor pull_resistor_10 (.node(pull_resistor_10_node));
  or or_3 (or_3_out, IDMEM_USER_BANK_B, IREAD_ENABLE_B);
  Pull_Resistor pull_resistor_11 (.node(pull_resistor_11_node));
  nor nor_2 (nor_2_out, IDMEM_USER_BANK_B, IWRITE_ENABLE);
  or or_4 (or_4_out, IDMEM_KERNAL_MODE_B, IREAD_ENABLE_B);
  not not_16 (not_16_out, RESET);
  not not_17 (not_17_out, VP_B);
  not not_18 (not_18_out, IWRITE_ENABLE);
  not not_19 (not_19_out, VP_B);
  not not_20 (not_20_out, RESET);
  or or_5 (or_5_out, IDMEM_OUT_INTERRUPTS_B, IREAD_ENABLE_B);
  nor nor_3 (nor_3_out, IDMEM_OUT_INTERRUPTS_B, IWRITE_ENABLE);
  or or_6 (or_6_out, not_16_out, not_17_out, nor_4_out);
  nor nor_4 (nor_4_out, not_18_out, IDMEM_KERNAL_MODE_B);
  or or_7 (or_7_out, D[0], not_19_out, not_20_out);
  Pull_Resistor pull_resistor_12 (.node(pull_resistor_12_node));
  Pull_Resistor pull_resistor_13 (.node({A8_15, A0_7}));
  // _8_bit_Latch__LVC573 8_bit_latch_lvc573_2: pin names not known; wires that end beside it: pull_resistor_10_node, microprocessor_w65c816_1_p8, BANK_LATCH, BA0_7
  // _8_bit_Bus_Transceiver__LVC4245 8_bit_bus_transceiver_lvc4245_1: pin names not known; wires that end beside it: DATA_TRANS_B, microprocessor_w65c816_1_p8, READ, D
  // _8_bit_Latch__LVC573 8_bit_latch_lvc573_3: pin names not known; wires that end beside it: pull_resistor_11_node, D, nor_2_out, USER_BANK
  D_Flip_Flop #(.trigger("high")) d_ff_1 (
    .clk(or_6_out), .D(or_7_out), .Q(KERNAL_MODE), .Qn(KERNAL_MODE_B));  // open: preset, reset
  // _8_bit_Latch__LVC573 8_bit_latch_lvc573_4: pin names not known; wires that end beside it: pull_resistor_12_node, D, nor_3_out, OUT_INTERRUPTS
  // Probe on BA0_7
  // Probe on D
  // _16_bit_Line_Driver__LVC16244 16_bit_line_driver_lvc16244_1: pin names not known; wires that end beside it: or_3_out, or_3_out, or_4_out, or_4_out, USER_BANK[7:4], USER_BANK[3:0], 4'b0000, {3'b000, KERNAL_MODE}, D[7:4], D[3:0], D[7:4], D[3:0]
  // _4_bit_Line_Driver__LVC126 4_bit_line_driver_lvc126_1: pin names not known; wires that end beside it: KERNAL_MODE_B, KERNAL_MODE, 1'b1, BA0_7[0], IRAM_A[16], IRAM_A[16]
  // _16_bit_Line_Driver__LVC16244 16_bit_line_driver_lvc16244_2: pin names not known; wires that end beside it: KERNAL_MODE, KERNAL_MODE, KERNAL_MODE, KERNAL_MODE, USER_BANK[7:4], USER_BANK[3:0], BA0_7[7:4], BA0_7[3:0], IRAM_A[15:12], IRAM_A[11:8], IRAM_A[7:4], IRAM_A[3:0]
  // _16_bit_Line_Driver__LVC16244 16_bit_line_driver_lvc16244_3: pin names not known; wires that end beside it: KERNAL_MODE_B, KERNAL_MODE_B, KERNAL_MODE_B, KERNAL_MODE_B, A8_15[7:4], A8_15[3:0], IRAM_A0_7[7:4], IRAM_A0_7[3:0], IRAM_A[15:12], IRAM_A[11:8], IRAM_A[7:4], IRAM_A[3:0]
  nand nand_8 (nand_8_out, DEVICE_B, A_128K, IREAD_ENABLE);
  nand nand_9 (nand_9_out, DEVICE_B, A_128K, IWRITE_ENABLE);
  // Probe on IRAM_A
  RAM #(.addrWidth(17), .databus("bidir"), .enables("line"), .trigger("high"), .\type ("nonvolatile")) ram_1 (
    .addr(IRAM_A), .data(D));  // open: we, oe, clk
  // NOT_Gate not_21 has open pins: in=nand_8_out, out=open
  // NOT_Gate not_22 has open pins: in=nand_9_out, out=open
  Pull_Resistor pull_resistor_14 (.node(pull_resistor_14_node));
  // NOT_Gate not_23 has open pins: in=pull_resistor_14_node, out=open
  // Probe on USER_BANK
  // Probe on KERNAL_MODE
  // _16_bit_Line_Driver__LVC16244 16_bit_line_driver_lvc16244_4: pin names not known; wires that end beside it: or_5_out, or_5_out, n16_bit_line_driver_lvc16244_4_p3, n16_bit_line_driver_lvc16244_4_p4, n16_bit_line_driver_lvc16244_4_p3, n16_bit_line_driver_lvc16244_4_p4, OUT_INTERRUPTS[7:4], OUT_INTERRUPTS[3:0], D[7:4], D[3:0], D[7:4], D[3:0]
  // Probe on OUT_INTERRUPTS
  // Probe on D
  and and_10 (and_10_out, A_128K_B, KERNAL_MODE, VALID_ADDRESS);
  and and_11 (and_11_out, VALID_ADDRESS, KERNAL_MODE_B);
  // _8_bit_Latch__LVC573 8_bit_latch_lvc573_5: pin names not known; wires that end beside it: KERNAL_MODE, D, BANK_MAP, MRAM_A16_23
  // _8_bit_Line_Driver__LVC541 8_bit_line_driver_lvc541_2: pin names not known; wires that end beside it: KERNAL_MODE_B, KERNAL_MODE_B, BA0_7, MRAM_A16_23
  // Probe on MRAM_A16_23
  nor nor_5 (MRAM_VALID_B, and_10_out, and_11_out);
  or or_8 (MRAM_VALID, and_10_out, and_11_out);
  or or_9 (or_9_out, IREAD_ENABLE_B, MRAM_VALID_B);
  or or_10 (or_10_out, IWRITE_ENABLE_B, MRAM_VALID_B);
  Pull_Resistor #(.pull("X")) pull_resistor_15 (.node(pull_resistor_15_node));
  Pull_Resistor pull_resistor_16 (.node(pull_resistor_16_node));
  // _8_bit_Bi_latch__LVC543 8_bit_bi_latch_lvc543_1: pin names not known; wires that end beside it: pull_resistor_15_node, or_10_out, pull_resistor_16_node, D, n8_bit_bi_latch_lvc543_1_p5, or_9_out, n8_bit_bi_latch_lvc543_1_p7, n8_bit_bi_latch_lvc543_1_p8
  // _16_bit_Line_Driver__LVC16244 16_bit_line_driver_lvc16244_5: pin names not known; wires that end beside it: MRAM_ACCESS_B, MRAM_ACCESS_B, MRAM_ACCESS_B, {RDY, MRAM_VALID, WRITE, READ}, MRAM_A16_23[3:0], MRAM_A16_23[7:4], {MREADY, MVALID, MWRITE, MREAD}, MRAM_A[19:16], MRAM_A[23:20]
  // _16_bit_Line_Driver__LVC16244 16_bit_line_driver_lvc16244_6: pin names not known; wires that end beside it: MRAM_ACCESS_B, MRAM_ACCESS_B, MRAM_ACCESS_B, MRAM_ACCESS_B, A8_15[7:4], A8_15[3:0], A0_7[7:4], A0_7[3:0], MRAM_A[15:12], MRAM_A[11:8], MRAM_A[7:4], MRAM_A[3:0]
  Pull_Resistor #(.pull("X")) pull_resistor_17 (.node(n8_bit_bi_latch_lvc543_1_p5));
  Pull_Resistor pull_resistor_18 (.node(n8_bit_bi_latch_lvc543_1_p7));
  // Probe on MRAM_A
  Pull_Resistor pull_resistor_19 (.node(pull_resistor_19_node));
  Pull_Resistor #(.pull(1)) pull_resistor_20 (.node(pull_resistor_20_node));
  nand nand_10 (nand_10_out, MREAD, MVALID);
  nand nand_11 (nand_11_out, MWRITE, MVALID);
  // _3_to_8_Decoder__LVC138 3_to_8_decoder_lvc138_3: pin names not known; wires that end beside it: CS0_B, pull_resistor_19_node, pull_resistor_19_node, MRAM_A[23:21], pull_resistor_20_node, {n3_to_8_decoder_lvc138_3_p6, CS3_B, CS2_B, CS1_B, CS0_B}
  Pull_Resistor #(.pull(1)) pull_resistor_21 (.node(pull_resistor_21_node));
  // Probe on MRAM_A[20:0]
  RAM #(.addrWidth(21), .databus("bidir"), .enables("line"), .trigger("high"), .\type ("nonvolatile")) ram_2 (
    .addr(MRAM_A[20:0]), .data(ram_2_data));  // open: we, oe, clk
  // NOT_Gate not_24 has open pins: in=nand_10_out, out=open
  // NOT_Gate not_25 has open pins: in=nand_11_out, out=open
  // NOT_Gate not_26 has open pins: in=pull_resistor_21_node, out=open
  RAM #(.addrWidth(21), .databus("bidir"), .enables("line"), .trigger("high"), .\type ("nonvolatile")) ram_3 (
    .addr(MRAM_A[20:0]), .data(n8_bit_bi_latch_lvc543_1_p8));  // open: we, oe, clk
  // NOT_Gate not_27 has open pins: in=nand_10_out, out=open
  // NOT_Gate not_28 has open pins: in=nand_11_out, out=open
  // NOT_Gate not_29 has open pins: in=CS1_B, out=open
  RAM #(.addrWidth(21), .databus("bidir"), .enables("line"), .trigger("high"), .\type ("nonvolatile")) ram_4 (
    .addr(MRAM_A[20:0]), .data(n8_bit_bi_latch_lvc543_1_p8));  // open: we, oe, clk
  // NOT_Gate not_30 has open pins: in=nand_10_out, out=open
  // NOT_Gate not_31 has open pins: in=nand_11_out, out=open
  // NOT_Gate not_32 has open pins: in=CS2_B, out=open
  RAM #(.addrWidth(21), .databus("bidir"), .enables("line"), .trigger("high"), .\type ("nonvolatile")) ram_5 (
    .addr(MRAM_A[20:0]), .data(n8_bit_bi_latch_lvc543_1_p8));  // open: we, oe, clk
  // NOT_Gate not_33 has open pins: in=nand_10_out, out=open
  // NOT_Gate not_34 has open pins: in=nand_11_out, out=open
  // NOT_Gate not_35 has open pins: in=CS3_B, out=open

  // Other names for the same wires on the sheet: IRAM_A16 = BA0_7[0]; RWB = READ; DEVICE_A0_3[3:0] = A0_7[3:0];
  //   MRAM_A0_7[7:0] = A0_7; DEVICE_N0_6[6:0] = {A8_15[2:0], A0_7[7:4]}; IRAM_A8_15[7:0] = A8_15;
  //   MRAM_A8_15[7:0] = A8_15; MRAM_A0_20[20:0] = MRAM_A[20:0]

  // Notes on the sheet:
  //   Interrupt Vectorring
  //   Device Decode (F000 to F7FF)
  //   Bank Decode
  //   Internal Device Select
  //   IDevice0 Address Select
endmodule

module Timing_Circuit (
  output [9:0] SELECTOR,
  output RST,
  output RST_1,
  output CLK,
  output CLK_B
);

  wire and_1_out, and_2_out, clock_1_out, nand_1_out, nand_2_out, pull_resistor_1_node, pull_resistor_2_node,
       pull_resistor_3_node, pull_resistor_4_node, pull_resistor_5_node, pull_resistor_6_node,
       pull_resistor_7_node, pull_resistor_8_node;
  wire [3:0] n4_bit_counter_lvc163_1_p7, n4_bit_counter_lvc163_2_p7;
  wire [7:5] n3_to_8_decoder_lvc138_1_p5, n3_to_8_decoder_lvc138_2_p5;

  Clock clock_1 (.out(clock_1_out));
  // EconoReset__DS1813 econoreset_ds1813_1: pin names not known; wires that end beside it: clock_1_out, RST
  Clock clock_2 (.out(CLK));
  not not_1 (CLK_B, CLK);
  D_Flip_Flop d_ff_1 (.clk(CLK), .D(RST), .Q(RST_1));  // open: Qn, preset, reset
  and and_1 (and_1_out, RST, nand_1_out);
  Pull_Resistor #(.pull(1)) pull_resistor_1 (.node(pull_resistor_1_node));
  Pull_Resistor #(.pull(1)) pull_resistor_2 (.node(pull_resistor_2_node));
  Pull_Resistor #(.pull(1)) pull_resistor_3 (.node(pull_resistor_3_node));
  and and_2 (and_2_out, RST, nand_2_out);
  Pull_Resistor #(.pull(1)) pull_resistor_4 (.node(pull_resistor_4_node));
  Pull_Resistor #(.pull(1)) pull_resistor_5 (.node(pull_resistor_5_node));
  Pull_Resistor #(.pull(1)) pull_resistor_6 (.node(pull_resistor_6_node));
  // _4_bit_Counter__LVC163 4_bit_counter_lvc163_1: pin names not known; wires that end beside it: and_1_out, pull_resistor_1_node, pull_resistor_2_node, CLK_B, pull_resistor_3_node, RST_1, n4_bit_counter_lvc163_1_p7
  // _4_bit_Counter__LVC163 4_bit_counter_lvc163_2: pin names not known; wires that end beside it: and_2_out, pull_resistor_4_node, pull_resistor_5_node, CLK, pull_resistor_6_node, RST_1, n4_bit_counter_lvc163_2_p7
  nand nand_1 (nand_1_out, ~n4_bit_counter_lvc163_1_p7[0], ~n4_bit_counter_lvc163_1_p7[1], n4_bit_counter_lvc163_1_p7[2], ~n4_bit_counter_lvc163_1_p7[3]);  // NAND_Gate
  nand nand_2 (nand_2_out, ~n4_bit_counter_lvc163_2_p7[0], ~n4_bit_counter_lvc163_2_p7[1], n4_bit_counter_lvc163_2_p7[2], ~n4_bit_counter_lvc163_2_p7[3]);  // NAND_Gate
  Pull_Resistor pull_resistor_7 (.node(pull_resistor_7_node));
  Pull_Resistor pull_resistor_8 (.node(pull_resistor_8_node));
  // _3_to_8_Decoder__LVC138 3_to_8_decoder_lvc138_1: pin names not known; wires that end beside it: pull_resistor_7_node, pull_resistor_7_node, n4_bit_counter_lvc163_1_p7[2:0], RST, {n3_to_8_decoder_lvc138_1_p5, SELECTOR[8], SELECTOR[6], SELECTOR[4], SELECTOR[2], SELECTOR[0]}
  // _3_to_8_Decoder__LVC138 3_to_8_decoder_lvc138_2: pin names not known; wires that end beside it: pull_resistor_8_node, pull_resistor_8_node, n4_bit_counter_lvc163_2_p7[2:0], RST_1, {n3_to_8_decoder_lvc138_2_p5, SELECTOR[7], SELECTOR[5], SELECTOR[3], SELECTOR[1], SELECTOR[9]}
  Pull_Resistor #(.pull(1)) pull_resistor_9 (.node(n3_to_8_decoder_lvc138_1_p5[5]));
  Pull_Resistor #(.pull(1)) pull_resistor_10 (.node(n3_to_8_decoder_lvc138_1_p5[6]));
  Pull_Resistor #(.pull(1)) pull_resistor_11 (.node(n3_to_8_decoder_lvc138_1_p5[7]));
  Pull_Resistor #(.pull(1)) pull_resistor_12 (.node(n3_to_8_decoder_lvc138_2_p5[5]));
  Pull_Resistor #(.pull(1)) pull_resistor_13 (.node(n3_to_8_decoder_lvc138_2_p5[6]));
  Pull_Resistor #(.pull(1)) pull_resistor_14 (.node(n3_to_8_decoder_lvc138_2_p5[7]));
  // Digital_Oscilloscope #(.nState(16)) digital_oscilloscope_1: pin names not known; wires that end beside it: CLK, SELECTOR[0], SELECTOR[1], SELECTOR[2], SELECTOR[3], SELECTOR[4], SELECTOR[5], SELECTOR[6], SELECTOR[7], SELECTOR[8], SELECTOR[9]

  // Other names for the same wires on the sheet: CLOCK_B = CLK_B; RESET_0 = RST; RESET_1 = RST_1
endmodule
